// Digital circuit AddSub8-ovf.dig as structural Verilog
module AddSub8_ovf (
  input  [7:0] AS,
  input  [7:0] B,
  input  [7:0] A,
  output [7:0] R,
  output OVF
);

  wire add8_1_p4, xnor_1_out, xor_2_out;
  wire [7:0] xor_1_out;

  assign xor_1_out = B ^ AS;  // XOr xor_1, 8 bits wide
  // Add8 add8_1: pin names not known; wires that end beside it: A, xor_1_out, AS[0], add8_1_p4, R
  xnor xnor_1 (xnor_1_out, A[7], xor_1_out[7]);
  xor xor_2 (xor_2_out, R[7], xnor_1_out);
  and and_1 (OVF, add8_1_p4, xor_2_out);
endmodule
